// Logisim project DLD project.circ as structural Verilog: 1 circuit, main circuit main
module main (
  input  A,
  input  B,
  input  C,
  input  D,
  output a_2,
  output b_2,
  output c_2,
  output d_2,
  output e,
  output f,
  output g
);

  wire and_1_out, and_2_out, and_3_out, and_4_out, and_5_out, and_6_out, and_7_out, and_8_out, and_9_out,
       and_10_out, and_11_out, and_12_out, and_13_out, and_14_out, and_15_out, and_16_out, and_17_out,
       clock_1_out, not_1_out, not_2_out, not_3_out, not_4_out, not_5_out, not_6_out, not_7_out, not_8_out,
       not_9_out, not_10_out, not_11_out, not_12_out, not_13_out, not_14_out, not_15_out, not_16_out,
       not_17_out, not_18_out, not_19_out, not_20_out, not_21_out, not_22_out, or_8_out;

  not not_1 (not_1_out, B);
  not not_2 (not_2_out, D);
  not not_3 (not_3_out, C);
  not not_4 (not_4_out, D);
  not not_5 (not_5_out, C);
  not not_6 (not_6_out, B);
  not not_7 (not_7_out, D);
  not not_8 (not_8_out, B);
  not not_9 (not_9_out, D);
  not not_10 (not_10_out, C);
  not not_11 (not_11_out, B);
  not not_12 (not_12_out, D);
  not not_13 (not_13_out, D);
  not not_14 (not_14_out, C);
  not not_15 (not_15_out, D);
  not not_16 (not_16_out, C);
  not not_17 (not_17_out, D);
  not not_18 (not_18_out, B);
  not not_19 (not_19_out, C);
  not not_20 (not_20_out, D);
  and and_1 (and_1_out, not_1_out, not_2_out);
  and and_2 (and_2_out, B, D);
  not not_21 (not_21_out, B);
  and and_3 (and_3_out, not_3_out, not_4_out);
  and and_4 (and_4_out, C, D);
  or or_1 (c_2, not_5_out, D, B);
  and and_5 (and_5_out, not_6_out, not_7_out);
  and and_6 (and_6_out, not_8_out, C);
  and and_7 (and_7_out, C, not_9_out);
  and and_8 (and_8_out, B, not_10_out, D);
  and and_9 (and_9_out, not_11_out, not_12_out);
  and and_10 (and_10_out, C, not_13_out);
  and and_11 (and_11_out, not_14_out, not_15_out);
  and and_12 (and_12_out, B, not_16_out);
  and and_13 (and_13_out, B, not_17_out);
  and and_14 (and_14_out, not_18_out, C);
  and and_15 (and_15_out, B, not_19_out);
  and and_16 (and_16_out, B, not_20_out);
  or or_2 (a_2, and_1_out, C, and_2_out, A);
  or or_3 (b_2, not_21_out, and_3_out, and_4_out);
  or or_4 (d_2, and_5_out, and_6_out, and_7_out, and_8_out, A);
  or or_5 (e, and_9_out, and_10_out);
  or or_6 (f, and_11_out, and_12_out, and_13_out, A);
  or or_7 (g, and_14_out, and_15_out, and_16_out, A);
  _7_Segment_Display u_7_segment_display_1 (.g(g), .f(f), .a(a_2), .b(b_2), .e(e), .d(d_2), .c(c_2), .dp(1'b0));
  Clock clock_1 (.out(clock_1_out));
  and and_17 (and_17_out, clock_1_out, or_8_out);
  not not_22 (not_22_out, or_8_out);
  or or_8 (or_8_out, D, C, B, A);
  LED led_1 (.in(and_17_out));
  LED led_2 (.in(or_8_out));
  LED led_3 (.in(not_22_out));

  // Notes on the sheet:
  //   NURSYAFIQAH BINTI SOBRI (1914338)
  //   DROPBOX DELIVERY SYSTEM
endmodule
